// Logisim project ALU.circ as structural Verilog: 6 circuits, main circuit main
module main (
  input  OPCODE_0,
  input  OPCODE_1,
  input  OPCODE_2,
  input  ALT_OPCODE,
  input  INPUT0_0,
  input  INPUT0_1,
  input  INPUT0_2,
  input  INPUT0_3,
  input  INPUT1_0,
  input  INPUT1_1,
  input  INPUT1_2,
  input  INPUT1_3,
  output OUTPUT0_0,
  output OUTPUT0_1,
  output OUTPUT0_2,
  output OUTPUT0_3,
  output OUTPUT1_0,
  output OUTPUT1_1,
  output OUTPUT1_2,
  output OUTPUT1_3,
  output CARRY,
  output NEGATIVE,
  output OVERFLOW,
  output ZERO
);

  Demultiplexer #(.select(3)) demultiplexer_1 (
    .in(1'b1), .sel({OPCODE_2, OPCODE_1, OPCODE_0}));  // open: out0, out1, out2, out3, out4, out5, out6, out7

  // Notes on the sheet:
  //   DMX gets 3 bit input
endmodule

module half_adder (
  input  INPUT_0,
  input  INPUT_1,
  output RESULT,
  output CARRY
);

  xor xor_1 (RESULT, INPUT_0, INPUT_1);
  and and_1 (CARRY, INPUT_0, INPUT_1);
endmodule

module full_adder_1_bit (
  input  INPUT_0,
  input  INPUT_1,
  input  CARRY_IN,
  output SUM,
  output CARRY_OUT
);

  wire half_adder_1_carry, half_adder_1_result, half_adder_2_carry;

  half_adder half_adder_1 (
    .INPUT_0(INPUT_0), .INPUT_1(INPUT_1), .RESULT(half_adder_1_result), .CARRY(half_adder_1_carry));
  half_adder half_adder_2 (.INPUT_0(half_adder_1_result), .INPUT_1(CARRY_IN), .RESULT(SUM), .CARRY(half_adder_2_carry));
  or or_1 (CARRY_OUT, half_adder_2_carry, half_adder_1_carry);
endmodule

module adder_4_bit (
  input  INPUT0_0,
  input  INPUT1_0,
  input  INPUT0_1,
  input  INPUT1_1,
  input  INPUT0_2,
  input  INPUT1_2,
  input  INPUT0_3,
  input  INPUT1_3,
  output OUT_0,
  output OUT_1,
  output OUT_2,
  output OUT_3,
  output CARRY
);

  wire full_adder_1_bit_1_carry_out, full_adder_1_bit_2_carry_out, full_adder_1_bit_3_carry_out;

  full_adder_1_bit full_adder_1_bit_1 (
    .INPUT_0(INPUT0_0), .INPUT_1(INPUT1_0), .SUM(OUT_0), .CARRY_OUT(full_adder_1_bit_1_carry_out));  // open: CARRY_IN
  full_adder_1_bit full_adder_1_bit_2 (
    .INPUT_0(INPUT0_1), .INPUT_1(INPUT1_1), .CARRY_IN(full_adder_1_bit_1_carry_out), .SUM(OUT_1),
    .CARRY_OUT(full_adder_1_bit_2_carry_out));
  full_adder_1_bit full_adder_1_bit_3 (
    .INPUT_0(INPUT0_2), .INPUT_1(INPUT1_2), .CARRY_IN(full_adder_1_bit_2_carry_out), .SUM(OUT_2),
    .CARRY_OUT(full_adder_1_bit_3_carry_out));
  full_adder_1_bit full_adder_1_bit_4 (
    .INPUT_0(INPUT0_3), .INPUT_1(INPUT1_3), .CARRY_IN(full_adder_1_bit_3_carry_out), .SUM(OUT_3),
    .CARRY_OUT(CARRY));
endmodule

module operator_normal (
  input  OP0,
  input  OP1,
  input  OP2,
  input  OP3,
  input  OP4,
  input  OP5,
  input  OP6,
  input  OP7,
  input  IN0_0,
  input  IN1_0,
  input  IN0_1,
  input  IN1_1,
  input  IN2_0,
  input  IN2_1,
  input  IN3_0,
  input  IN3_1,
  output OUT0_0,
  output OUT0_1,
  output OUT0_2,
  output OUT0_3,
  output OUT1_0,
  output OUT1_1,
  output OUT1_2,
  output OUT1_3,
  output CARRY,
  output NEGATIVE,
  output OVERFLOW,
  output ZERO
);

  wire [7:0] and_1_out, bit_extender_1_out;

  assign bit_extender_1_out = {{7{OP0}}, OP0};  // Bit_Extender bit_extender_1
  assign and_1_out = bit_extender_1_out & {IN3_1, IN3_0, IN2_1, IN2_0, IN1_1, IN0_1, IN1_0, IN0_0};  // AND_Gate and_1, 8 bits wide
  adder_4_bit adder_4_bit_1 (
    .INPUT0_0(and_1_out[0]), .INPUT1_0(and_1_out[1]), .INPUT0_1(and_1_out[2]), .INPUT1_1(and_1_out[3]),
    .INPUT0_2(and_1_out[4]), .INPUT1_2(and_1_out[5]), .INPUT0_3(and_1_out[6]), .INPUT1_3(and_1_out[7]),
    .OUT_0(CARRY), .OUT_1(CARRY), .OUT_2(CARRY), .OUT_3(CARRY), .CARRY(CARRY));
  assign {OUT1_3, OUT1_2, OUT1_1, OUT1_0} = {{3{1'b0}}, CARRY};  // Bit_Extender bit_extender_2

  assign OUT0_0 = CARRY;
  assign OUT0_1 = CARRY;
  assign OUT0_2 = CARRY;
  assign OUT0_3 = CARRY;
  assign ZERO = CARRY;

  // Other names for the same wires on the sheet: to_NEGATIVE = NEGATIVE; to_CARRY = CARRY; to_OUT0[3:0] = {4{CARRY}};
  //   to_ZERO = CARRY; to_OUT1[3:0] = {OUT1_3, OUT1_2, OUT1_1, OUT1_0}; to_OVERFLOW = OVERFLOW; to_sub = OP1

  // Notes on the sheet:
  //   OPx = Input from opcode DMX
  //   zero check
endmodule

module operator_alternate (
  input  OP0,
  input  OP1,
  input  OP2,
  input  OP3,
  input  OP4,
  input  OP5,
  input  OP6,
  input  OP7,
  input  IN0_0,
  input  IN1_0,
  input  IN0_1,
  input  IN1_1,
  input  IN2_0,
  input  IN2_1,
  input  IN3_0,
  input  IN3_1,
  output OUT0_0,
  output OUT0_1,
  output OUT0_2,
  output OUT0_3,
  output OUT1_0,
  output OUT1_1,
  output OUT1_2,
  output OUT1_3,
  output CARRY
);

  wire [7:0] and_1_out, bit_extender_1_out;

  assign bit_extender_1_out = {{7{OP0}}, OP0};  // Bit_Extender bit_extender_1
  assign and_1_out = bit_extender_1_out & {IN3_1, IN3_0, IN2_1, IN2_0, IN1_1, IN0_1, IN1_0, IN0_0};  // AND_Gate and_1, 8 bits wide
  adder_4_bit adder_4_bit_1 (
    .INPUT0_0(and_1_out[0]), .INPUT1_0(and_1_out[1]), .INPUT0_1(and_1_out[2]), .INPUT1_1(and_1_out[3]),
    .INPUT0_2(and_1_out[4]), .INPUT1_2(and_1_out[5]), .INPUT0_3(and_1_out[6]), .INPUT1_3(and_1_out[7]));  // open: OUT_0, OUT_1, OUT_2, OUT_3, CARRY

  // Other names for the same wires on the sheet: to_sub = OP1

  // Notes on the sheet:
  //   OPx = Input from opcode DMX
endmodule
